// Logisim project ADD_5.circ as structural Verilog
module ADD_4 (
  input  A,
  input  B,
  input  C,
  output S0,
  output S1,
  output S2,
  output S3,
  output S4,
  output S5,
  output S6,
  output S7
);

  and and_1 (S0, ~A, ~A, ~A);  // AND_Gate
  and and_2 (S1, ~A, ~B, C);  // AND_Gate
  and and_3 (S2, ~A, B, ~C);  // AND_Gate
  and and_4 (S3, A, ~B, ~C);  // AND_Gate
  and and_5 (S4, ~A, B, C);  // AND_Gate
  and and_6 (S5, A, ~B, C);  // AND_Gate
  and and_7 (S6, A, B, ~C);  // AND_Gate
  and and_8 (S7, A, B, C);
endmodule
