// Logisim project ADD_7.circ as structural Verilog: 2 circuits, main circuit main
module main (
  input  A,
  input  B,
  input  C,
  input  D
);

  wire add_7_1_a_2, add_7_1_b_2, add_7_1_c_2, add_7_1_d_2, add_7_1_e, add_7_1_f, add_7_1_g;

  ADD_7 add_7_1 (
    .a_2(add_7_1_a_2), .b_2(add_7_1_b_2), .c_2(add_7_1_c_2), .d_2(add_7_1_d_2), .e(add_7_1_e), .f(add_7_1_f),
    .g(add_7_1_g), .A(A), .B(B), .C(C), .D(D));
  _7_Segment_Display u_7_segment_display_1 (
    .g(add_7_1_g), .f(add_7_1_f), .a(add_7_1_a_2), .b(add_7_1_b_2), .e(add_7_1_e), .d(add_7_1_d_2),
    .c(add_7_1_c_2));  // open: dp
endmodule

module ADD_7 (
  input  A,
  input  B,
  input  C,
  input  D,
  output a_2,
  output b_2,
  output c_2,
  output d_2,
  output e,
  output f,
  output g
);

  wire and_1_out, and_2_out, and_3_out, and_4_out, and_5_out, and_6_out, and_7_out, and_8_out, and_9_out,
       and_10_out, and_11_out, and_12_out, xnor_1_out, xnor_2_out;

  xnor xnor_1 (xnor_1_out, D, C);
  or or_1 (c_2, B, ~C, D);  // OR_Gate
  and and_1 (and_1_out, ~D, ~B);  // AND_Gate
  and and_2 (and_2_out, ~B, C);  // AND_Gate
  and and_3 (and_3_out, C, ~D);  // AND_Gate
  and and_4 (and_4_out, B, ~C, D);  // AND_Gate
  and and_5 (and_5_out, ~B, ~D);  // AND_Gate
  and and_6 (and_6_out, C, ~D);  // AND_Gate
  and and_7 (and_7_out, ~C, ~D);  // AND_Gate
  and and_8 (and_8_out, B, ~C);  // AND_Gate
  and and_9 (and_9_out, B, ~D);  // AND_Gate
  and and_10 (and_10_out, B, ~C);  // AND_Gate
  and and_11 (and_11_out, ~B, C);  // AND_Gate
  and and_12 (and_12_out, C, ~D);  // AND_Gate
  xnor xnor_2 (xnor_2_out, D, B);
  or or_2 (a_2, xnor_2_out, A, C);
  or or_3 (b_2, xnor_1_out, ~B);  // OR_Gate
  or or_4 (e, and_5_out, and_6_out);
  or or_5 (f, A, and_7_out, and_8_out, and_9_out);
  or or_6 (g, A, and_10_out, and_11_out, and_12_out);
  or or_7 (d_2, A, and_1_out, and_2_out, and_3_out, and_4_out);
endmodule
