// Logisim project BCD_7_Seg.circ as structural Verilog: 2 circuits, main circuit main
module main (
  input  in_1,
  input  in_2,
  input  in_3
);

  wire bcd_7_seg_1_a_2, bcd_7_seg_1_b_2, bcd_7_seg_1_c_2, bcd_7_seg_1_d, bcd_7_seg_1_e, bcd_7_seg_1_f,
       bcd_7_seg_1_g, bcd_7_seg_2_a_2, bcd_7_seg_2_b_2, bcd_7_seg_2_c_2, bcd_7_seg_2_d, bcd_7_seg_2_e,
       bcd_7_seg_2_f, bcd_7_seg_2_g, clock_1_out;
  wire [2:0] counter_1_q;

  BCD_7_Seg bcd_7_seg_1 (
    .a_2(bcd_7_seg_1_a_2), .b_2(bcd_7_seg_1_b_2), .c_2(bcd_7_seg_1_c_2), .d(bcd_7_seg_1_d),
    .e(bcd_7_seg_1_e), .f(bcd_7_seg_1_f), .g(bcd_7_seg_1_g), .A(in_1), .B(in_2), .c(in_3));
  _7_Segment_Display u_7_segment_display_1 (
    .g(bcd_7_seg_1_g), .f(bcd_7_seg_1_f), .a(bcd_7_seg_1_a_2), .b(bcd_7_seg_1_b_2), .e(bcd_7_seg_1_e),
    .d(bcd_7_seg_1_d), .c(bcd_7_seg_1_c_2));  // open: dp
  Counter #(.width(3), .max('h7)) counter_1 (.Q(counter_1_q), .clk(clock_1_out));  // open: load, D, count, carry, clr
  Clock clock_1 (.out(clock_1_out));
  BCD_7_Seg bcd_7_seg_2 (
    .a_2(bcd_7_seg_2_a_2), .b_2(bcd_7_seg_2_b_2), .c_2(bcd_7_seg_2_c_2), .d(bcd_7_seg_2_d),
    .e(bcd_7_seg_2_e), .f(bcd_7_seg_2_f), .g(bcd_7_seg_2_g), .A(counter_1_q[2]), .B(counter_1_q[1]),
    .c(counter_1_q[0]));
  _7_Segment_Display u_7_segment_display_2 (
    .g(bcd_7_seg_2_g), .f(bcd_7_seg_2_f), .a(bcd_7_seg_2_a_2), .b(bcd_7_seg_2_b_2), .e(bcd_7_seg_2_e),
    .d(bcd_7_seg_2_d), .c(bcd_7_seg_2_c_2));  // open: dp
endmodule

module BCD_7_Seg (
  input  A,
  input  B,
  input  c,
  output a_2,
  output b_2,
  output c_2,
  output d,
  output e,
  output f,
  output g
);

  and and_1 (g, ~A, ~B);  // AND_Gate
  or or_1 (b_2, B, ~c);  // OR_Gate
  or or_2 (d, A, c);
  or or_3 (e, c, ~B);  // OR_Gate
  or or_4 (a_2, g, c);

  assign c_2 = b_2;
  assign f = e;
endmodule
