// Logisim project Luz.circ as structural Verilog: 2 circuits, main circuit main
module main (
);

  wire clock_1_out, luz_1_l1, luz_1_l2, luz_1_l3, luz_1_l4, luz_1_l5, luz_1_l6, luz_1_l7;
  wire [2:0] random_1_out;

  Clock clock_1 (.out(clock_1_out));
  luz luz_1 (
    .A(random_1_out), .L1(luz_1_l1), .L2(luz_1_l2), .L3(luz_1_l3), .L4(luz_1_l4), .L5(luz_1_l5),
    .L6(luz_1_l6), .L7(luz_1_l7));
  Random #(.width(3)) random_1 (.clk(clock_1_out), .out(random_1_out));  // open: next, clr
  LED led_1 (.in(luz_1_l1));
  LED led_2 (.in(luz_1_l2));
  LED led_3 (.in(luz_1_l3));
  LED led_4 (.in(luz_1_l5));
  LED led_5 (.in(luz_1_l4));
  LED led_6 (.in(luz_1_l6));
  LED led_7 (.in(luz_1_l7));
endmodule

module luz (
  input  [2:0] A,
  output L1,
  output L2,
  output L3,
  output L4,
  output L5,
  output L6,
  output L7
);

  or or_1 (L1, A[1], A[2]);
  and and_1 (L2, A[2], A[1]);

  assign L3 = A[2];
  assign L4 = A[0];
  assign L5 = A[2];
  assign L6 = L2;
  assign L7 = L1;
endmodule
