// Logisim project aula_laboratorio.circ as structural Verilog: 3 circuits, main circuit main
module main (
  input  [3:0] in_1,
  input  [3:0] in_2,
  output [3:0] out_3,
  output [3:0] out_4,
  output out_5,
  output [3:0] out_6
);

  ADD add_1 (.Overflow(out_5), .B(in_2), .A(in_1), .in_3(1'b0), .out_5(out_6));
  // Probe on out_6

  assign out_3 = in_1;
  assign out_4 = in_2;
endmodule

module ADD (
  input  [3:0] B,
  input  [3:0] A,
  input  in_3,
  output Overflow,
  output [3:0] out_5
);

  wire add1_2_vai_1, add1_3_vai_1, add1_4_vai_1;

  // Probe on B
  ADD1 add1_1 (.A(A[3]), .B(B[3]), .Vem_1(add1_3_vai_1), .S(out_5[3]), .Vai_1(Overflow));
  // Probe on out_5
  // Probe on A
  ADD1 add1_2 (.A(A[1]), .B(B[1]), .Vem_1(add1_4_vai_1), .S(out_5[1]), .Vai_1(add1_2_vai_1));
  ADD1 add1_3 (.A(A[2]), .B(B[2]), .Vem_1(add1_2_vai_1), .S(out_5[2]), .Vai_1(add1_3_vai_1));
  ADD1 add1_4 (.A(A[0]), .B(B[0]), .Vem_1(in_3), .S(out_5[0]), .Vai_1(add1_4_vai_1));
endmodule

module ADD1 (
  input  A,
  input  B,
  input  Vem_1,
  output S,
  output Vai_1
);

  wire and_1_out, and_2_out, and_3_out, xor_1_out;

  xor xor_1 (xor_1_out, A, B);
  and and_1 (and_1_out, A, Vem_1);
  and and_2 (and_2_out, A, B);
  and and_3 (and_3_out, B, Vem_1);
  xor xor_2 (S, xor_1_out, Vem_1);
  or or_1 (Vai_1, and_1_out, and_2_out, and_3_out);
endmodule
